# Fritzing sketch wiring_fritzing (saved by Fritzing 1.0.6)
breadboards: 1

parts:
  Part2 = InvenSense MPU6050
  A1 = Raspberry Pi Pico2
  Part3 = Motor Driver 1A Dual TB6612FNG
  BAT1 = Battery Holders [package=lipo-1100mAh]
  A2 = Raspberry Pi 5
  DC_Mot_Enc2 = DC Motor with two-phase hall-encoder [part_number=VT-E-G25A-06-177E]
  DC_Mot_Enc1 = DC Motor with two-phase hall-encoder [part_number=VT-E-G25A-06-177E]

nets:
  VCC: Part2.VCC, A1.pin_36, Part3.VCC
  GND: Part2.GND, A1.pin_3, A1.pin_8, A1.pin_13, A1.pin_18, A1.pin_23, A1.pin_28, A1.pin_33, A1.pin_38, A1.pin_42, Part3.GND, Part3.PWMB, BAT1.-, A2.GND, A2.Fan-GND, DC_Mot_Enc2.pin4, DC_Mot_Enc1.pin4
  N1: Part2.SCL, A1.pin_22
  N2: Part2.SDA, A1.pin_21
  N3: A1.pin_14, Part3.BIN2
  N4: A1.pin_15, Part3.BIN1
  N5: A1.pin_16, Part3.STBY
  N6: A1.pin_17, Part3.AIN1
  N7: A1.pin_19, Part3.AIN2
  N8: A1.pin_20, Part3.PWMA
  N9: A1.pin_24, DC_Mot_Enc1.pin5
  N10: A1.pin_25, DC_Mot_Enc1.pin6
  N11: A1.pin_26, DC_Mot_Enc2.pin5
  N12: A1.pin_27, DC_Mot_Enc2.pin6
  N13: Part3.B01, DC_Mot_Enc2.pin2
  N14: Part3.B02, DC_Mot_Enc2.pin1
  N15: Part3.A02, DC_Mot_Enc1.pin2
  N16: Part3.A01, DC_Mot_Enc1.pin1
  N17: Part3.VM, BAT1.+
  N18: A2.5V, DC_Mot_Enc2.pin3, DC_Mot_Enc1.pin3

notes:
  left motor
  right motor
  Motor +
  Motor -
  Encoder +
  Encoder -
  Phase A
  Phase B
  6x AA 7.2V

custom parts:
  Raspberry Pi Pico2: Raspberry Pi Pico 2W is our new $7 microcontroller board, built on RP2350: our new high-performance, secure microcontroller with on board WiFi.
  Motor Driver 1A Dual TB6612FNG: The TB6612FNG motor driver can control up to two DC motors at a constant current of 1.2A (3.2A peak). Two input signals (IN1 and IN2) can be used to control the motor in one of four function modes - CW, CCW, short-brake, and stop. The two motor outputs (A and B) can be separately controlled, the speed of each motor is controlled via a PWM input signal with a frequency up to 100kHz. The STBY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
  Raspberry Pi 5: The RPi5, a faster version of the awesome Raspberry Pi4B ARM Board with 40 pin gpio.
